# Fritzing sketch Smart_Door_Bell_using_Blynk (saved by Fritzing 0.9.4)
breadboards: 1

parts:
  ESP32_-_Back2 = ESP32 - CAM
  DFRobot_DFPlayer_Mini2 = DFRobot DFPlayer Mini [part_number=DFR0299]
  S2 = Pushbutton [package="[THT]"]
  R4 = Resistor [tolerance=±5% resistance=1k package="2512 [SMD]"]
  R5 = Resistor [tolerance=±5% resistance=47k package="2512 [SMD]"]
  R6 = Resistor [tolerance=±5% resistance=220 package="2512 [SMD]"]
  LED2 = LED - 5mm [color="Blue (430nm)" package="5 mm [THT]"]
  SP2 = SPEAKER [package=pcb_mount_speaker]

nets:
  N1: ESP32_-_Back2.GPIO14, S2.Pin_3, S2.Pin_4
  N2: ESP32_-_Back2.GPIO15, LED2.anode
  N3: ESP32_-_Back2.GPIO13, DFRobot_DFPlayer_Mini2.TX
  N4: ESP32_-_Back2.GPIO12, R4.Pin_0
  N5: ESP32_-_Back2.GND#7, DFRobot_DFPlayer_Mini2.GND-1, DFRobot_DFPlayer_Mini2.GND-2, R5.Pin_0, R6.Pin_0
  5V: ESP32_-_Back2.5V, DFRobot_DFPlayer_Mini2.VCC
  N6: DFRobot_DFPlayer_Mini2.RX, R4.Pin_1
  N7: DFRobot_DFPlayer_Mini2.SPK_1, SP2.-
  N8: DFRobot_DFPlayer_Mini2.SPK_2, SP2.+
  N9: S2.Pin_1, S2.Pin_2, R5.Pin_1
  N10: R6.Pin_1, LED2.cathode

custom parts:
  ESP32 - CAM: The ESP32-CAM has a very competitive small-size camera module that can operate independently as a minimum system with a footprint of only 27*40.5*4.5mm and a deep sleep current of up to 6mA.
